# Fritzing sketch sketch (saved by Fritzing 0.9.3b)
breadboards: 1
stripboards: 1

parts:
  元件2 = Arduino Nano (Rev3.0)
  R1 = Resistor [tolerance=±5% resistance=100k package=THT]
  S1 = Pushbutton [package="[SMD]"]
  S2 = Pushbutton [package="[SMD]"]
  R2 = Resistor [tolerance=±5% resistance=100k package=THT]
  S3 = Pushbutton [package="[SMD]"]
  R3 = Resistor [tolerance=±5% resistance=100k package=THT]
  S4 = Pushbutton [package="[SMD]"]
  S5 = Pushbutton [package="[SMD]"]
  R4 = Resistor [tolerance=±5% resistance=100k package=THT]
  R5 = Resistor [tolerance=±5% resistance=100k package=THT]
  LED1 = LED - 5mm [color="Red (633nm)" package="5 mm [THT]"]
  R6 = Resistor [tolerance=±5% resistance=1k package=THT]
  元件1 = Arduino Uno (Rev3) - ICSP
  SG1 = Buzzer 12mm [package=buzzer-12mm-ns]
  LED2 = LED - 5mm [color="Red (633nm)" package="5 mm [THT]"]
  LED4 = LED - 5mm [color="Blue (430nm)" package="5 mm [THT]"]
  R7 = Resistor [tolerance=±5% resistance=1k package=THT]
  R8 = Resistor [tolerance=±5% resistance=1k package=THT]
  R9 = Resistor [tolerance=±5% resistance=1k package=THT]
  LED3 = smd LED [color="Green (560nm)" package="0603 [SMD]"]

nets:
  N1: 元件2.RESET, 元件2.5V, 元件1.RESET
  N2: 元件2.D2, R7.Pin_0
  N3: 元件2.D3, R8.Pin_0
  N4: 元件2.D4, R9.Pin_0
  N5: 元件2.D10, SG1.1
  N6: 元件2.D11/MOSI, 元件1.D2
  N7: 元件2.D12/MISO, 元件1.D3_PWM
  N8: R1.Pin_0, S1.Pin_1, S1.Pin_2, 元件1.D10_PWM/SS
  N9: R1.Pin_1, R2.Pin_1, R3.Pin_1, R4.Pin_1, R5.Pin_0
  N10: S1.Pin_3, S1.Pin_4, S2.Pin_3, S2.Pin_4, S3.Pin_3, S3.Pin_4, S4.Pin_3, S4.Pin_4, S5.Pin_1, S5.Pin_2, LED1.cathode, 元件1.5V
  N11: S2.Pin_1, S2.Pin_2, R2.Pin_0, 元件1.D8
  N12: S3.Pin_1, S3.Pin_2, R3.Pin_0, 元件1.D5_PWM
  N13: S4.Pin_1, S4.Pin_2, R4.Pin_0, 元件1.D6_PWM
  N14: S5.Pin_3, S5.Pin_4, R5.Pin_1, 元件1.D7
  N15: LED1.anode, R6.Pin_0
  N16: R6.Pin_1, 元件1.D4
  N17: SG1.2, LED2.cathode, LED4.cathode, LED3.cathode
  N18: LED2.anode, R9.Pin_1
  N19: LED4.anode, R7.Pin_1
  N20: R8.Pin_1, LED3.anode
